// Logisim project Circuito.circ as structural Verilog: 1 circuit, main circuit main
module main (
  input  A,
  input  B,
  output out_3,
  output out_4,
  output out_5,
  output out_6,
  output out_7,
  output out_8
);

  wire and_1_out, nand_1_out, nor_1_out, not_1_out, not_3_out, or_1_out;

  not not_1 (not_1_out, A);
  not not_2 (out_3, not_1_out);
  not not_3 (not_3_out, B);
  not not_4 (out_4, not_3_out);
  nand nand_1 (nand_1_out, A, B);
  not not_5 (out_5, nand_1_out);
  nor nor_1 (nor_1_out, A, B);
  not not_6 (out_6, nor_1_out);
  and and_1 (and_1_out, A, B);
  not not_7 (out_7, and_1_out);
  or or_1 (or_1_out, A, B);
  not not_8 (out_8, or_1_out);

  // Notes on the sheet:
  //   NOT
  //   NAND
  //   NOR
  //   AND
  //   OR
endmodule
